# Fritzing sketch TSFRL_master_module (saved by Fritzing 0.9.0b)

parts:
  Part1 = Arduino Nano (Rev3.0)
  IC1 = Voltage Regulator [package=to220-igo]
  U1 = MAX485 [package=dil08]
  C1 = Capacitor Polarized [package=cpol-radial-100uf-25v]
  C2 = Capacitor Polarized [package=cpol-radial-10uf-25v]
  R1 = Resistor [tolerance=±5% resistance=220 package=THT]
  POWER = LED - 3mm [color="Red (633nm)" package="3 mm [THT]"]
  J1 = rounded female pin header, 8 pins [form="♀ (female rounded)"]
  IC2 = Hex Inverter Schmitt Trigger SN74HC14 [package="DIP (Dual Inline)"]
  J2 = male pin header, 5 pins [form="♂ (male)"]  # not connected

nets:
  GND: Part1.GND, IC1.GND, U1.GND, C1.-, C2.-, POWER.cathode, J1.pin1, IC2.GND
  5V: Part1.5V, R1.Pin_1, POWER.anode, IC2.VCC
  12V: IC1.IN, C1.+
  N1: IC1.OUT, C2.+, R1.Pin_0

notes:
  TSFRL_master_module_keys
  8) +5v
  7) keyUP
  6) keyRIGHT
  5) keyLEFT
  4) keyDOWN
  3)keySTART
  2)keySTOP/CANCEL
  1)GND
